# Fritzing sketch AxoControllerV2 (saved by Fritzing 0.9.3b)
breadboards: 1

parts:
  WeMos_D1_Mini1 = WeMos D1 Mini  # not connected
  IC2 = IC, DIP package, 8 pins [chip_label=MAX604 part_number=MAX604]
  J1 = male pin header, 4 pins [form="♂ (male)"]
  DS1 = DS18B20 1-Wire Temperature Sensor [part_number=DS18B20]
  R1 = Resistor [tolerance=±5% resistance=4.7k package=THT]

nets:
  N1: IC2.pin1, IC2.pin4, J1.pin2
  N2: IC2.pin2, IC2.pin5, IC2.pin6, J1.pin1, DS1.GND, R1.Pin_0
  N3: IC2.pin8, DS1.VDD
  N4: DS1.DQ, R1.Pin_1

notes:
  3V3
  12V
  Cnt
  Sens
